# Fritzing sketch das ist der schaltplan fuer das dingen (saved by Fritzing 0.9.3b)
breadboards: 1

parts:
  Bauteil1 = Arduino Uno (Rev3)
  R1 = Resistor [tolerance=±5% resistance=100 package="2010 [SMD]"]
  RHT1 = Humidity and Temperature Sensor RHT03

nets:
  N1: Bauteil1.D7, R1.Pin_1, RHT1.Vcc
  N2: Bauteil1.5V, R1.Pin_0, RHT1.Data-signal
  N3: Bauteil1.GND, RHT1.GND_1
